# Fritzing sketch MacroPad (saved by Fritzing 0.9.9b)

parts:
  Part1 = Arduino Pro Micro (Clone)
  S2 = Pushbutton [package="[SMD]"]
  S3 = Pushbutton [package="[SMD]"]
  S5 = Pushbutton [package="[SMD]"]
  S6 = Pushbutton [package="[SMD]"]
  S7 = Pushbutton [package="[SMD]"]
  S8 = Pushbutton [package="[SMD]"]
  S9 = Pushbutton [package="[SMD]"]
  S10 = Pushbutton [package="[SMD]"]
  S11 = Pushbutton [package="[SMD]"]
  S12 = Pushbutton [package="[SMD]"]
  S13 = Pushbutton [package="[SMD]"]
  RE1 = Rotary Encoder [package=THT]
  RE2 = Rotary Encoder [package=THT]
  S15 = Pushbutton [package="[SMD]"]
  S16 = Pushbutton [package="[SMD]"]
  S19 = Pushbutton [package="[SMD]"]
  S20 = Pushbutton [package="[SMD]"]
  S22 = Pushbutton [package="[SMD]"]
  S24 = Pushbutton [package="[SMD]"]
  S25 = Pushbutton [package="[SMD]"]
  S26 = Pushbutton [package="[SMD]"]
  S27 = Pushbutton [package="[SMD]"]
  D1 = Diode [package=diode-hv]
  D2 = Diode [package=diode-hv]
  D7 = Diode [package=diode-hv]
  D8 = Diode [package=diode-hv]
  D9 = Diode [package=diode-hv]
  D10 = Diode [package=diode-hv]
  D12 = Diode [package=diode-hv]
  D13 = Diode [package=diode-hv]
  D14 = Diode [package=diode-hv]
  D15 = Diode [package=diode-hv]
  D17 = Diode [package=diode-hv]
  D18 = Diode [package=diode-hv]
  D19 = Diode [package=diode-hv]
  D20 = Diode [package=diode-hv]
  D22 = Diode [package=diode-hv]
  D23 = Diode [package=diode-hv]
  D24 = Diode [package=diode-hv]
  D25 = Diode [package=diode-hv]
  R1 = Resistor [tolerance=±5% resistance=2.2k package="0603 [SMD]"]
  R2 = Resistor [tolerance=±5% resistance=2.2k package="0603 [SMD]"]  # not connected
  R3 = Resistor [tolerance=±5% resistance=2.2k package="0603 [SMD]"]
  R4 = Resistor [tolerance=±5% resistance=2.2k package="0603 [SMD]"]
  R5 = Resistor [tolerance=±5% resistance=2.2k package="0603 [SMD]"]

nets:
  N1: Part1.GND, Part1.D14, Part1.D15, RE1.EncoderPinC, RE2.EncoderPinC, S15.Pin_1, S15.Pin_2, S16.Pin_3, S16.Pin_4, R5.Pin_1
  N2: Part1.D2, S19.Pin_3, S19.Pin_4, S20.Pin_3, S20.Pin_4, S22.Pin_3, S22.Pin_4, S27.Pin_3, S27.Pin_4, D8.A, D10.C, D13.A, D15.C, D18.A, D20.C, D23.A, D25.C
  N3: Part1.D3, S5.Pin_3, S5.Pin_4, S8.Pin_3, S8.Pin_4, S12.Pin_3, S12.Pin_4, S24.Pin_3, S24.Pin_4, D7.C, D10.A, D12.C, D15.A, D17.C, D20.A, D22.C, D25.A
  N4: Part1.D4, S3.Pin_3, S3.Pin_4, S7.Pin_3, S7.Pin_4, S10.Pin_3, S10.Pin_4, S13.Pin_3, S13.Pin_4, S26.Pin_3, S26.Pin_4, D1.C, D2.A, D7.A, D9.C, D12.A, D14.C, D17.A, D19.C, D22.A, D24.C
  N5: Part1.D5, S2.Pin_3, S2.Pin_4, S6.Pin_3, S6.Pin_4, S9.Pin_3, S9.Pin_4, S11.Pin_3, S11.Pin_4, S25.Pin_3, S25.Pin_4, D1.A, D9.A, D14.A, D19.A, D24.A
  N6: Part1.D6, D23.C, R4.Pin_1, R5.Pin_0
  N7: Part1.D7, D18.C, R3.Pin_1
  N8: Part1.D8, D13.C, R3.Pin_0
  N9: Part1.D9, D8.C, R1.Pin_1
  N10: Part1.D10, D2.C, R1.Pin_0
  N11: Part1.A0, RE1.EncoderPinA
  N12: Part1.A1, RE1.EncoderPinB
  N13: Part1.A2, RE2.EncoderPinA
  N14: Part1.A3, RE2.EncoderPinB

notes:
  Mechanical Switches displayed as momentary switched
  Rotary Encoders with momentary switches
